# Fritzing sketch Yukita_Diagram_V0.1.0 (saved by Fritzing 0.9.0b)
breadboards: 1

parts:
  Part1 = Arduino Ethernet Shield (Rev3)
  LED1 = smd LED [color="Red (633nm)" package="0805 [SMD]"]

nets:
  N1: Part1.GND, LED1.anode
  N2: Part1.PWM_D3, LED1.cathode

notes:
  Router --- Ethernet Cable ------------
