# Fritzing sketch Yukita_Diagram_V0.2.0 (saved by Fritzing 0.9.0b)
breadboards: 1

parts:
  Part1 = Arduino Ethernet Shield (Rev3)
  LX = smd LED [color="White (8000K)" package="1206 [SMD]"]
  LX_2 = smd LED [color="White (4500K)" package="1206 [SMD]"]
  plowDwn = smd LED [color="Red (660nm)" package="1206 [SMD]"]
  plowUp = smd LED [color="Red (660nm)" package="1206 [SMD]"]
  leftMotor = smd LED [color="Yellow (595nm)" package="1206 [SMD]"]
  rightMotor = smd LED [color="Yellow (595nm)" package="1206 [SMD]"]

nets:
  N1: Part1.PWM_D9, plowUp.anode
  N2: Part1.PWM_D11, LX.anode, LX_2.anode
  N3: Part1.GND, LX.cathode, LX_2.cathode, plowDwn.cathode, plowUp.cathode, leftMotor.cathode, rightMotor.cathode
  N4: Part1.PWM_D3, rightMotor.anode
  N5: Part1.PWM_D5, leftMotor.anode
  N6: Part1.PWM_D6, plowDwn.anode
